# Fritzing sketch Umanoide Sketch (saved by Fritzing 0.9.3b)
circuit board: 7.02306cm x 7.21517cm
stripboards: 15

parts:
  R2 = Basic Servo
  R3 = Basic Servo
  R4 = Basic Servo
  R0 = Basic Servo
  R6 = Basic Servo
  R8 = Basic Servo
  L8 = Basic Servo
  R7 = Basic Servo
  L7 = Basic Servo
  R5 = Basic Servo
  L0 = Basic Servo
  L4 = Basic Servo
  L5 = Basic Servo
  L3 = Basic Servo
  L1 = Basic Servo
  L2 = Basic Servo
  LM1 = RioRand LM2596
  L6 = Basic Servo
  C0 = Basic Servo
  L9 = Basic Servo
  R9 = Basic Servo
  R1 = Basic Servo
  Part1 = Arduino Pro Mini (3.3V)
  U5 = 74HC4017 [package="DIP16 [THT]"]
  Componente4 = Bluetooth HC-05 Macho
  GY2 = MPU-6050 Board GY-521 [form="♀ (female)" package=THT]
  U6 = 74HC4017 [package="DIP16 [THT]"]

nets:
  GND: R2.gnd, R3.gnd, R4.gnd, R0.gnd, R6.gnd, R8.gnd, L8.gnd, R7.gnd, L7.gnd, R5.gnd, L0.gnd, L4.gnd, L5.gnd, L3.gnd, L1.gnd, L2.gnd, LM1.Pin_3, L6.gnd, C0.gnd, L9.gnd, R9.gnd, R1.gnd, Part1.GND, U5.GND, U5./CP1, Componente4.GND, GY2.pin2, U6.GND
  VCC: R2.vcc, R3.vcc, R4.vcc, R0.vcc, R6.vcc, R8.vcc, R7.vcc, L7.vcc, R5.vcc, L0.vcc, L4.vcc, L5.vcc, L3.vcc, L1.vcc, L2.vcc, LM1.Pin_2, L6.vcc, C0.vcc, R9.vcc, R1.vcc
  N1: R2.pulse, U5.Q2
  N2: R3.pulse, U5.Q3
  N3: R4.pulse, U5.Q4
  N4: R0.pulse, U5.Q0
  N5: R6.pulse, U5.Q6
  N6: R8.pulse, U5.Q8
  VCC_2: L8.vcc, L9.vcc
  N7: L8.pulse, U6.Q8
  N8: R7.pulse, U5.Q7
  N9: L7.pulse, U6.Q7
  N10: R5.pulse, U5.Q5
  N11: L0.pulse, U6.Q0
  N12: L4.pulse, U6.Q4
  N13: L5.pulse, U6.Q5
  N14: L3.pulse, U6.Q3
  N15: L1.pulse, U6.Q1
  N16: L2.pulse, U6.Q2
  N17: L6.pulse, U6.Q6
  N18: L9.pulse, U6.Q9
  N19: R9.pulse, U5.Q9
  N20: R1.pulse, U5.Q1
  VCC_3: Part1.VCC, U5.VCC, Componente4.VCC, GY2.pin1, U6.VCC
  N21: Part1.A4, GY2.pin4
  N22: Part1.A5, GY2.pin3
  N23: Part1.SCK, U6.MR
  N24: Part1.MISO, U5.MR
  N25: Part1.D10, U6.CP0
  N26: Part1.D9, U5.CP0
  N27: Part1.RXI, Componente4.TXD
  N28: Part1.TXO, Componente4.RXD

custom parts:
  74HC4017: 5-stage Johnson decade counter
  MPU-6050 Board GY-521: Acelerometro y Giroscopio MPU-6050 Board GY-521
